# Fritzing sketch wiring (saved by Fritzing 1.0.4)
breadboards: 1

parts:
  R3 = Resistor [tolerance=±5% power=0.25W resistance=4.7k package=THT]
  DS1 = DS18B20 1-Wire Temperature Sensor Probe
  DS2 = DS18B20 1-Wire Temperature Sensor Probe
  DS3 = DS18B20 1-Wire Temperature Sensor Probe
  DS4 = DS18B20 1-Wire Temperature Sensor Probe
  Q2 = NPN-Transistor [part_number=2N3904 package="TO92 [THT]"]
  R4 = Resistor [tolerance=±5% power=0.25W resistance=1k package=THT]
  R1 = Resistor [tolerance=±5% power=0.25W resistance=47k package=THT]
  R2 = Resistor [tolerance=±5% power=0.25W resistance=100 package=THT]
  Q1 = PNP-Transistor [part_number=2N3906 package="TO92 [THT]"]
  C1 = Electrolytic Capacitor [capacitance=3mF voltage=6.3V package="100 mil [THT, electrolytic]"]

nets:
  GPIO_22: R3.Pin_0, DS1.DQ, DS2.DQ, DS3.DQ, DS4.DQ
  VDD: R3.Pin_1, DS1.VDD, DS2.VDD, DS3.VDD, DS4.VDD, Q1.C
  GND: DS1.GND, DS2.GND, DS3.GND, DS4.GND, Q2.E, C1.-
  N1: Q2.B, R4.Pin_1
  N2: Q2.C, R2.Pin_0
  GPIO_23: R4.Pin_0
  N3: R1.Pin_0, R2.Pin_1, Q1.B
  3.3V: R1.Pin_1, Q1.E, C1.+
